# Fritzing sketch smart_thermostat (saved by Fritzing 0.8.5b)
circuit board: 9.21065cm x 5.48977cm
breadboards: 1

parts:
  R2 = Resistor [tolerance=±5% resistance=470 package=THT]
  R3 = Resistor [tolerance=±5% resistance=270 package=THT]
  R4 = Resistor [tolerance=±5% resistance=1k package=THT]
  R5 = Resistor [tolerance=±5% resistance=4.7k package=THT]
  C1 = Ceramic Capacitor [capacitance=100nF package="100 mil [THT, multilayer]"]
  C3 = Ceramic Capacitor [capacitance=22pF package="100 mil [THT, multilayer]"]
  C2 = Ceramic Capacitor [capacitance=22pF package="100 mil [THT, multilayer]"]
  D1 = Rectifier Diode [part_number=1N4001 package="300 mil [THT]"]
  X1 = Crystal [frequency="16 Mhz" package=THT]
  U1 = atmega328 [package=dip]
  T1 = NPN-Transistor [part_number=BC548 package="TO92 [THT]"]
  D2 = LED - 5mm [color="Red (633nm)" package="5 mm [THT]"]
  RF_Receiver = RF Receiver [chip_label=IC package="SIP (Single Inline) [THT]"]
  IC1 = DS18B20 [part_number=DS18B20 chip_label=IC package="SIP (Single Inline) [THT]"]
  R1 = Rotary Potentiometer (Small) [maximum_resistance=100kΩ package=THT]
  S1 = Pushbutton [package=THT]
  Furnace = female pin header, 2 pins [form="♀ (female)"]
  5Vin = female pin header, 2 pins [form="♀ (female)"]
  U2 = RELAY [package=relay-g5q]

nets:
  N1: R2.Pin_0, T1.B
  N2: R2.Pin_1, U1.D7
  N3: R3.Pin_0, U1.D8
  N4: R3.Pin_1, D2.anode
  5V: R4.Pin_0, R5.Pin_0, C1.0, D1.cathode, RF_Receiver.VCC, IC1.VCC, R1.leg2, 5Vin.pin2, U2.COIL1
  N5: R4.Pin_1, U1.RESET
  N6: R5.Pin_1, U1.D10_(PWM), IC1.Data
  GND: C1.1, C3.1, C2.0, U1.GND, T1.E, D2.cathode, RF_Receiver.Gnd, IC1.Gnd, R1.leg1, S1.leg1, 5Vin.pin1
  N7: C3.0, X1.pin_0, U1.XLAT2
  N8: C2.1, X1.pin_1, U1.XLAT1
  N9: D1.anode, T1.C, U2.COIL2
  N10: U1.D9_(PWM), S1.leg0
  N11: U1.D11_(PWM), RF_Receiver.Data
  N12: U1.A0, R1.wiper
  N13: Furnace.pin1, U2.MAIN
  N14: Furnace.pin2, U2.NO

custom parts:
  RF Receiver: 433 Mhz receiver module
  DS18B20: Dallas 1-wire digital temperature sensor
